// Logisim project 16-4 encoder.circ as structural Verilog: 1 circuit, main circuit 16-4 encoder
module _16_4_encoder (
  input  [15:0] X_prime_15_0,
  input  EI_prime,
  output [3:0] A_prime_3_0,
  output EO_prime,
  output GS_prime
);

  wire n8_3_encoder_1_gs_prime, n8_3_encoder_2_eo_prime;
  wire [2:0] n8_3_encoder_1_out_3, n8_3_encoder_2_out_3;

  _8_3_encoder u_8_3_encoder_1 (
    .EI_prime_1(n8_3_encoder_2_eo_prime), .EO_prime(EO_prime), .GS_prime(n8_3_encoder_1_gs_prime),
    .out_3(n8_3_encoder_1_out_3), .in_1(X_prime_15_0[7:0]));
  _8_3_encoder u_8_3_encoder_2 (
    .EI_prime_1(EI_prime), .EO_prime(n8_3_encoder_2_eo_prime), .GS_prime(A_prime_3_0[3]),
    .out_3(n8_3_encoder_2_out_3), .in_1(X_prime_15_0[15:8]));
  assign A_prime_3_0[2:0] = n8_3_encoder_1_out_3 & n8_3_encoder_2_out_3;  // AND_Gate and_1, 3 bits wide
  and and_2 (GS_prime, n8_3_encoder_1_gs_prime, A_prime_3_0[3]);

  // Notes on the sheet:
  //   Encoder 0
  //   Encoder 1
endmodule
