// Logisim project 16-bit BCLA-CLA adder.circ as structural Verilog: 1 circuit, main circuit 16-bit BCLA-CLA adder
module _16_bit_BCLA_CLA_adder (
  input  [15:0] A0_15,
  input  [15:0] B0_15,
  input  CI,
  output CO,
  output [15:0] S0_15
);

  wire [2:0] n4_bit_cla_1_c0_3;
  wire [3:0] n4_bit_bcla_adder_1_g_star, n4_bit_bcla_adder_1_p_star;

  _4_bit_BCLA_adder u_4_bit_bcla_adder_1 (
    .A0_3(A0_15[3:0]), .B0_3(B0_15[3:0]), .CI(CI), .G_star(n4_bit_bcla_adder_1_g_star[0]),
    .P_star(n4_bit_bcla_adder_1_p_star[0]), .S0_3(S0_15[3:0]));
  _4_bit_BCLA_adder u_4_bit_bcla_adder_2 (
    .A0_3(A0_15[7:4]), .B0_3(B0_15[7:4]), .CI(n4_bit_cla_1_c0_3[0]), .G_star(n4_bit_bcla_adder_1_g_star[1]),
    .P_star(n4_bit_bcla_adder_1_p_star[1]), .S0_3(S0_15[7:4]));
  _4_bit_BCLA_adder u_4_bit_bcla_adder_3 (
    .A0_3(A0_15[11:8]), .B0_3(B0_15[11:8]), .CI(n4_bit_cla_1_c0_3[1]),
    .G_star(n4_bit_bcla_adder_1_g_star[2]), .P_star(n4_bit_bcla_adder_1_p_star[2]), .S0_3(S0_15[11:8]));
  _4_bit_BCLA_adder u_4_bit_bcla_adder_4 (
    .A0_3(A0_15[15:12]), .B0_3(B0_15[15:12]), .CI(n4_bit_cla_1_c0_3[2]),
    .G_star(n4_bit_bcla_adder_1_g_star[3]), .P_star(n4_bit_bcla_adder_1_p_star[3]), .S0_3(S0_15[15:12]));
  _4_bit_CLA u_4_bit_cla_1 (
    .CI(CI), .G0_3(n4_bit_bcla_adder_1_g_star), .P0_3(n4_bit_bcla_adder_1_p_star),
    .C0_3({CO, n4_bit_cla_1_c0_3}));
endmodule
