// Logisim project 2-1 multiplexer.circ as structural Verilog: 1 circuit, main circuit 2-1 multiplexer
module _2_1_multiplexer (
  input  D0,
  input  A,
  input  D1,
  input  EN_prime,
  output Y
);

  wire and_1_out, and_2_out, not_1_out, not_2_out, or_1_out;

  not not_1 (not_1_out, A);
  and and_1 (and_1_out, D0, not_1_out);
  and and_2 (and_2_out, A, D1);
  not not_2 (not_2_out, EN_prime);
  or or_1 (or_1_out, and_1_out, and_2_out);
  and and_3 (Y, or_1_out, not_2_out);
endmodule
