// Logisim project 2-4 decoder.circ as structural Verilog: 1 circuit, main circuit 2-4 decoder
module _2_4_decoder (
  input  [1:0] I1_0,
  input  EN_prime,
  output [3:0] Y_prime_3_0
);

  wire not_1_out, not_2_out;

  not not_1 (not_1_out, I1_0[0]);
  not not_2 (not_2_out, I1_0[1]);
  or or_1 (Y_prime_3_0[0], I1_0[0], EN_prime, I1_0[1]);
  or or_2 (Y_prime_3_0[1], not_1_out, EN_prime, I1_0[1]);
  or or_3 (Y_prime_3_0[2], I1_0[0], EN_prime, not_2_out);
  or or_4 (Y_prime_3_0[3], not_1_out, EN_prime, not_2_out);

  // Notes on the sheet:
  //   I0
  //   I1
  //   Y0
  //   Y1
  //   Y2
  //   Y3
endmodule
