// Logisim project 3-8 decoder.circ as structural Verilog: 1 circuit, main circuit 3-8 decoder
module _3_8_decoder (
  input  [2:0] I2_0,
  input  EN_prime,
  output [7:0] Y_prime_7_0
);

  wire not_1_out;
  wire [3:0] bit_extender_1_out, n2_4_decoder_1_y_prime_3_0, n2_4_decoder_2_y_prime_3_0;

  not not_1 (not_1_out, I2_0[2]);
  assign bit_extender_1_out = {{3{EN_prime}}, EN_prime};  // Bit_Extender bit_extender_1
  _2_4_decoder u_2_4_decoder_1 (.I1_0(I2_0[1:0]), .EN_prime(I2_0[2]), .Y_prime_3_0(n2_4_decoder_1_y_prime_3_0));
  _2_4_decoder u_2_4_decoder_2 (.I1_0(I2_0[1:0]), .EN_prime(not_1_out), .Y_prime_3_0(n2_4_decoder_2_y_prime_3_0));
  assign Y_prime_7_0[3:0] = n2_4_decoder_1_y_prime_3_0 | bit_extender_1_out;  // OR_Gate or_1, 4 bits wide
  assign Y_prime_7_0[7:4] = n2_4_decoder_2_y_prime_3_0 | bit_extender_1_out;  // OR_Gate or_2, 4 bits wide

  // Notes on the sheet:
  //   Decoder 0
  //   Decoder 1
endmodule
