// Logisim project 4-1 multiplexer.circ as structural Verilog: 1 circuit, main circuit 4-1 multiplexer
module _4_1_multiplexer (
  input  D0,
  input  D1,
  input  A0,
  input  A1,
  input  D2,
  input  D3,
  input  EN_prime,
  output Y
);

  wire n2_1_multiplexer_1_y, n2_1_multiplexer_2_y, not_1_out, not_2_out, or_1_out;

  not not_1 (not_1_out, A1);
  not not_2 (not_2_out, EN_prime);
  _2_1_multiplexer u_2_1_multiplexer_1 (.D0(D0), .A(A0), .D1(D1), .Y(n2_1_multiplexer_1_y), .EN_prime(A1));
  _2_1_multiplexer u_2_1_multiplexer_2 (.D0(D2), .A(A0), .D1(D3), .Y(n2_1_multiplexer_2_y), .EN_prime(not_1_out));
  or or_1 (or_1_out, n2_1_multiplexer_1_y, n2_1_multiplexer_2_y);
  and and_1 (Y, or_1_out, not_2_out);

  // Notes on the sheet:
  //              MUX 0
  //              MUX 0
endmodule
