// Logisim project 4-10 decoder.circ as structural Verilog: 1 circuit, main circuit 4-10 decoder
module _4_10_decoder (
  input  [3:0] A0_3,
  output [9:0] Y_prime_0_9
);

  wire not_1_out, not_2_out, not_3_out, not_4_out;

  not not_1 (not_1_out, A0_3[0]);
  not not_2 (not_2_out, A0_3[1]);
  not not_3 (not_3_out, A0_3[2]);
  not not_4 (not_4_out, A0_3[3]);
  nand nand_1 (Y_prime_0_9[0], not_4_out, not_3_out, not_2_out, not_1_out);
  nand nand_2 (Y_prime_0_9[1], not_4_out, not_3_out, not_2_out, A0_3[0]);
  nand nand_3 (Y_prime_0_9[2], not_4_out, not_3_out, A0_3[1], not_1_out);
  nand nand_4 (Y_prime_0_9[3], not_4_out, not_3_out, A0_3[1], A0_3[0]);
  nand nand_5 (Y_prime_0_9[4], not_4_out, A0_3[2], not_2_out, not_1_out);
  nand nand_6 (Y_prime_0_9[5], not_4_out, A0_3[2], not_2_out, A0_3[0]);
  nand nand_7 (Y_prime_0_9[6], not_4_out, A0_3[2], A0_3[1], not_1_out);
  nand nand_8 (Y_prime_0_9[7], not_4_out, A0_3[2], A0_3[1], A0_3[0]);
  nand nand_9 (Y_prime_0_9[8], A0_3[3], not_3_out, not_2_out, not_1_out);
  nand nand_10 (Y_prime_0_9[9], A0_3[3], not_3_out, not_2_out, A0_3[0]);

  // Notes on the sheet:
  //   A0
  //   A1
  //   A2
  //   A3
  //   Y0'
  //   Y1'
  //   Y2'
  //   Y3'
  //   Y4'
  //   Y5'
  //   Y6'
  //   Y7'
  //   Y8'
  //   Y9'
endmodule
