// Logisim project 4-16 decoder.circ as structural Verilog: 1 circuit, main circuit 4-16 decoder
module _4_16_decoder (
  input  [3:0] I3_0,
  input  EN_prime,
  output [15:0] Y_prime_15_0
);

  wire not_1_out;
  wire [7:0] bit_extender_1_out, n3_8_decoder_1_y_prime_7_0, n3_8_decoder_2_y_prime_7_0;

  assign bit_extender_1_out = {{7{EN_prime}}, EN_prime};  // Bit_Extender bit_extender_1
  not not_1 (not_1_out, I3_0[3]);
  _3_8_decoder u_3_8_decoder_1 (.I2_0(I3_0[2:0]), .EN_prime(I3_0[3]), .Y_prime_7_0(n3_8_decoder_1_y_prime_7_0));
  _3_8_decoder u_3_8_decoder_2 (.I2_0(I3_0[2:0]), .EN_prime(not_1_out), .Y_prime_7_0(n3_8_decoder_2_y_prime_7_0));
  assign Y_prime_15_0[7:0] = n3_8_decoder_1_y_prime_7_0 | bit_extender_1_out;  // OR_Gate or_1, 8 bits wide
  assign Y_prime_15_0[15:8] = bit_extender_1_out | n3_8_decoder_2_y_prime_7_0;  // OR_Gate or_2, 8 bits wide
endmodule
