// Logisim project 4-2 encoder.circ as structural Verilog: 2 circuits, main circuit 4-2 encoder
module _4_2_encoder (
  input  [3:0] X_prime_3_0,
  input  EI_prime,
  output [1:0] A_prime_1_0,
  output EO_prime,
  output GS_prime
);

  wire and_1_out, and_2_out, not_1_out, not_2_out, not_3_out, or_1_out;

  or or_1 (or_1_out, X_prime_3_0[1], not_1_out);
  not not_1 (not_1_out, X_prime_3_0[2]);
  and and_1 (and_1_out, X_prime_3_0[2], X_prime_3_0[3]);
  not not_2 (not_2_out, EI_prime);
  and and_2 (and_2_out, or_1_out, X_prime_3_0[3]);
  or or_2 (A_prime_1_0[0], and_2_out, EI_prime);
  or or_3 (A_prime_1_0[1], and_1_out, EI_prime);
  nand nand_1 (EO_prime, X_prime_3_0[0], X_prime_3_0[1], X_prime_3_0[2], X_prime_3_0[3], not_2_out);
  not not_3 (not_3_out, EO_prime);
  or or_4 (GS_prime, not_3_out, EI_prime);

  // Notes on the sheet:
  //   EI'使能输入端低电平有效
  //   Xi‘输入低电平输入有效 
  //   Ai'输出为反码形式
  //   EO'输出使能端低电平有效，仅编码器工作且无编码输入信号时为低电平
  //   GS'组信号输出端低电平有效，仅编码器工作且有编码输入信号时为低电平
endmodule

module _4_2_encoder_auto (
  input  X0,
  input  X1,
  input  X2,
  input  X3,
  input  EI,
  output A0,
  output A1,
  output EO,
  output GS
);

  wire and_1_out, and_2_out, and_3_out, and_4_out, not_1_out, not_2_out, not_3_out, not_4_out, not_5_out;

  not not_1 (not_1_out, X2);
  and and_1 (and_1_out, X2, X3);
  not not_2 (not_2_out, X0);
  not not_3 (not_3_out, X1);
  not not_4 (not_4_out, X2);
  not not_5 (not_5_out, X3);
  and and_2 (and_2_out, X0, X1, X2, X3);
  and and_3 (and_3_out, not_1_out, X3);
  and and_4 (and_4_out, X1, X3);
  or or_1 (A1, EI, and_1_out);
  or or_2 (EO, not_2_out, not_3_out, not_4_out, not_5_out, EI);
  or or_3 (GS, EI, and_2_out);
  or or_4 (A0, EI, and_3_out, and_4_out);
endmodule
