// Logisim project 4-bit CLA adder.circ as structural Verilog: 1 circuit, main circuit 4-bit CLA adder
module _4_bit_CLA_adder (
  input  [3:0] A0_3,
  input  [3:0] B0_3,
  input  CI,
  output [3:0] S0_3,
  output CO
);

  wire [2:0] n4_bit_cla_1_c0_3;
  wire [3:0] cla_full_adder_1_gi, cla_full_adder_1_pi;

  CLA_full_adder cla_full_adder_1 (
    .Ai(A0_3[0]), .Bi(B0_3[0]), .Ci_1(CI), .Si(S0_3[0]), .Gi(cla_full_adder_1_gi[0]),
    .Pi(cla_full_adder_1_pi[0]));
  CLA_full_adder cla_full_adder_2 (
    .Ai(A0_3[1]), .Bi(B0_3[1]), .Ci_1(n4_bit_cla_1_c0_3[0]), .Si(S0_3[1]), .Gi(cla_full_adder_1_gi[1]),
    .Pi(cla_full_adder_1_pi[1]));
  CLA_full_adder cla_full_adder_3 (
    .Ai(A0_3[2]), .Bi(B0_3[2]), .Ci_1(n4_bit_cla_1_c0_3[1]), .Si(S0_3[2]), .Gi(cla_full_adder_1_gi[2]),
    .Pi(cla_full_adder_1_pi[2]));
  CLA_full_adder cla_full_adder_4 (
    .Ai(A0_3[3]), .Bi(B0_3[3]), .Ci_1(n4_bit_cla_1_c0_3[2]), .Si(S0_3[3]), .Gi(cla_full_adder_1_gi[3]),
    .Pi(cla_full_adder_1_pi[3]));
  _4_bit_CLA u_4_bit_cla_1 (
    .CI(CI), .G0_3(cla_full_adder_1_gi), .P0_3(cla_full_adder_1_pi), .C0_3({CO, n4_bit_cla_1_c0_3}));

  // Notes on the sheet:
  //   FA0
  //   FA1
  //   FA2
  //   FA3
endmodule
