// Logisim project 4-bit CLA.circ as structural Verilog: 1 circuit, main circuit 4-bit CLA
module _4_bit_CLA (
  input  CI,
  input  [3:0] G0_3,
  input  [3:0] P0_3,
  output [3:0] C0_3
);

  wire and_1_out, and_2_out, and_3_out, and_4_out, and_5_out, and_6_out, and_7_out, and_8_out, and_9_out,
       and_10_out;

  and and_1 (and_1_out, CI, P0_3[0]);
  and and_2 (and_2_out, P0_3[1], G0_3[0]);
  and and_3 (and_3_out, P0_3[0], P0_3[1], CI);
  and and_4 (and_4_out, P0_3[2], G0_3[1]);
  and and_5 (and_5_out, P0_3[2], P0_3[1], G0_3[0]);
  and and_6 (and_6_out, P0_3[2], P0_3[1], P0_3[0], CI);
  and and_7 (and_7_out, P0_3[3], G0_3[2]);
  and and_8 (and_8_out, P0_3[3], P0_3[2], G0_3[1]);
  and and_9 (and_9_out, P0_3[3], P0_3[2], P0_3[1], G0_3[0]);
  and and_10 (and_10_out, P0_3[3], P0_3[2], P0_3[1], P0_3[0], CI);
  or or_1 (C0_3[0], and_1_out, G0_3[0]);
  or or_2 (C0_3[1], G0_3[1], and_2_out, and_3_out);
  or or_3 (C0_3[2], G0_3[2], and_4_out, and_5_out, and_6_out);
  or or_4 (C0_3[3], G0_3[3], and_7_out, and_8_out, and_9_out, and_10_out);
endmodule
