// Logisim project 4-bit ripple carry adder.circ as structural Verilog: 1 circuit, main circuit 4-bit ripple carry adder
module _4_bit_ripple_carry_adder (
  input  [3:0] A0_3,
  input  [3:0] B0_3,
  input  CI,
  output CO,
  output [3:0] S0_3
);

  wire full_adder_1_ci, full_adder_2_ci, full_adder_3_ci;

  full_adder full_adder_1 (.Ai(A0_3[0]), .Bi(B0_3[0]), .Ci_1(CI), .Si(S0_3[0]), .Ci(full_adder_1_ci));
  full_adder full_adder_2 (.Ai(A0_3[1]), .Bi(B0_3[1]), .Ci_1(full_adder_1_ci), .Si(S0_3[1]), .Ci(full_adder_2_ci));
  full_adder full_adder_3 (.Ai(A0_3[2]), .Bi(B0_3[2]), .Ci_1(full_adder_2_ci), .Si(S0_3[2]), .Ci(full_adder_3_ci));
  full_adder full_adder_4 (.Ai(A0_3[3]), .Bi(B0_3[3]), .Ci_1(full_adder_3_ci), .Si(S0_3[3]), .Ci(CO));

  // Notes on the sheet:
  //   FA0
  //   FA1
  //   FA2
  //   FA3
endmodule
