// Logisim project 8-1 multiplexer.circ as structural Verilog: 1 circuit, main circuit 8-1 multiplexer
module _8_1_multiplexer (
  input  D0,
  input  D1,
  input  D2,
  input  D3,
  input  D4,
  input  D5,
  input  D6,
  input  D7,
  input  A0,
  input  A1,
  input  A2,
  input  EN_prime,
  output Y
);

  wire n4_1_multiplexer_1_y, n4_1_multiplexer_2_y, not_1_out, not_2_out, or_1_out;

  not not_1 (not_1_out, A2);
  not not_2 (not_2_out, EN_prime);
  _4_1_multiplexer u_4_1_multiplexer_1 (
    .D0(D0), .D1(D1), .A0(A0), .A1(A1), .D2(D2), .D3(D3), .EN_prime(A2), .Y(n4_1_multiplexer_1_y));
  _4_1_multiplexer u_4_1_multiplexer_2 (
    .D0(D4), .D1(D5), .A0(A0), .A1(A1), .D2(D6), .D3(D7), .EN_prime(not_1_out), .Y(n4_1_multiplexer_2_y));
  or or_1 (or_1_out, n4_1_multiplexer_1_y, n4_1_multiplexer_2_y);
  and and_1 (Y, or_1_out, not_2_out);

  // Notes on the sheet:
  //   MUX 4-1 0
  //   MUX 4-1 1
endmodule
