// Logisim project 8-3 encoder.circ as structural Verilog: 2 circuits, main circuit 8-3 encoder
module _8_3_encoder (
  input  [7:0] in_1,
  input  EI_prime_1,
  output [2:0] out_3,
  output EO_prime,
  output GS_prime
);

  wire n4_2_encoder_1_gs_prime, n4_2_encoder_2_eo_prime;
  wire [1:0] n4_2_encoder_1_a_prime_1_0, n4_2_encoder_2_a_prime_1_0;

  _4_2_encoder u_4_2_encoder_1 (
    .EO_prime(EO_prime), .EI_prime(n4_2_encoder_2_eo_prime), .GS_prime(n4_2_encoder_1_gs_prime),
    .X_prime_3_0(in_1[3:0]), .A_prime_1_0(n4_2_encoder_1_a_prime_1_0));
  _4_2_encoder u_4_2_encoder_2 (
    .EO_prime(n4_2_encoder_2_eo_prime), .EI_prime(EI_prime_1), .GS_prime(out_3[2]), .X_prime_3_0(in_1[7:4]),
    .A_prime_1_0(n4_2_encoder_2_a_prime_1_0));
  and and_1 (out_3[0], n4_2_encoder_1_a_prime_1_0[0], n4_2_encoder_2_a_prime_1_0[0]);
  and and_2 (out_3[1], n4_2_encoder_1_a_prime_1_0[1], n4_2_encoder_2_a_prime_1_0[1]);
  and and_3 (GS_prime, n4_2_encoder_1_gs_prime, out_3[2]);

  // Notes on the sheet:
  //   Encoder 0
  //   Encoder 1
endmodule

module _8_3_encoder_auto (
  input  X0,
  input  X1,
  input  X2,
  input  X3,
  input  X4,
  input  X5,
  input  X6,
  input  X7,
  input  EI1,
  output A0,
  output A1,
  output A2,
  output EO,
  output GS
);

  wire and_1_out, and_2_out, and_3_out, and_4_out, and_5_out, and_6_out, and_7_out, and_8_out, and_9_out,
       not_1_out, not_2_out, not_3_out, not_4_out, not_5_out, not_6_out, not_7_out, not_8_out, not_9_out,
       not_10_out, not_11_out, not_12_out, not_13_out;

  not not_1 (not_1_out, X6);
  not not_2 (not_2_out, X4);
  not not_3 (not_3_out, X2);
  not not_4 (not_4_out, X4);
  not not_5 (not_5_out, X5);
  and and_1 (and_1_out, X4, X5, X6, X7);
  not not_6 (not_6_out, X0);
  not not_7 (not_7_out, X1);
  not not_8 (not_8_out, X2);
  not not_9 (not_9_out, X3);
  not not_10 (not_10_out, X4);
  not not_11 (not_11_out, X5);
  not not_12 (not_12_out, X6);
  not not_13 (not_13_out, X7);
  and and_2 (and_2_out, X0, X1, X2, X3, X4, X5, X6, X7);
  and and_3 (and_3_out, not_1_out, X7);
  and and_4 (and_4_out, not_2_out, X5, X7);
  and and_5 (and_5_out, not_3_out, X3, X5, X7);
  and and_6 (and_6_out, X1, X3, X5, X7);
  and and_7 (and_7_out, not_4_out, X6, X7);
  and and_8 (and_8_out, not_5_out, X6, X7);
  and and_9 (and_9_out, X2, X3, X6, X7);
  or or_1 (A2, EI1, and_1_out);
  or or_2 (EO, not_6_out, not_7_out, not_8_out, not_9_out, not_10_out, not_11_out, not_12_out, not_13_out, EI1);
  or or_3 (GS, EI1, and_2_out);
  or or_4 (A0, EI1, and_3_out, and_4_out, and_5_out, and_6_out);
  or or_5 (A1, EI1, and_7_out, and_8_out, and_9_out);
endmodule
