// Logisim project 8-bit CLA ripple adder.circ as structural Verilog: 1 circuit, main circuit 8-bit CLA ripple adder
module _8_bit_CLA_ripple_adder (
  input  [7:0] A0_7,
  input  [7:0] B0_7,
  input  CI,
  output [7:0] S0_7,
  output CO
);

  wire n4_bit_cla_adder_1_co;

  _4_bit_CLA_adder u_4_bit_cla_adder_1 (
    .A0_3(A0_7[3:0]), .B0_3(B0_7[3:0]), .CI(CI), .S0_3(S0_7[3:0]), .CO(n4_bit_cla_adder_1_co));
  _4_bit_CLA_adder u_4_bit_cla_adder_2 (
    .A0_3(A0_7[7:4]), .B0_3(B0_7[7:4]), .CI(n4_bit_cla_adder_1_co), .S0_3(S0_7[7:4]), .CO(CO));

  // Notes on the sheet:
  //   CLAA0
  //   CLAA1
endmodule
