// Logisim project CLA full-adder.circ as structural Verilog: 1 circuit, main circuit CLA full-adder
module CLA_full_adder (
  input  Ai,
  input  Bi,
  input  Ci_1,
  output Si,
  output Gi,
  output Pi
);

  xor xor_1 (Pi, Ai, Bi);
  xor xor_2 (Si, Pi, Ci_1);
  and and_1 (Gi, Ai, Bi);
endmodule
