// Logisim project bcd-7-seg driver decoder.circ as structural Verilog: 1 circuit, main circuit bcd-7-seg driver decoder
module bcd_7_seg_driver_decoder (
  input  [3:0] DCBA,
  output [6:0] gfedcba
);

  wire and_1_out, and_2_out, and_3_out, and_4_out, and_5_out, and_6_out, and_7_out, and_8_out, and_9_out,
       and_10_out, not_1_out, not_2_out, not_3_out;

  not not_1 (not_1_out, DCBA[0]);
  not not_2 (not_2_out, DCBA[1]);
  not not_3 (not_3_out, DCBA[2]);
  and and_1 (and_1_out, not_3_out, DCBA[1]);
  and and_2 (and_2_out, not_1_out, not_3_out);
  and and_3 (and_3_out, DCBA[0], DCBA[2]);
  and and_4 (and_4_out, not_1_out, not_2_out);
  and and_5 (and_5_out, DCBA[0], DCBA[1]);
  or or_1 (gfedcba[2], not_2_out, DCBA[0], DCBA[2]);
  and and_6 (and_6_out, DCBA[1], not_1_out);
  and and_7 (and_7_out, not_3_out, DCBA[3]);
  and and_8 (and_8_out, not_2_out, DCBA[2]);
  and and_9 (and_9_out, not_1_out, DCBA[2]);
  or or_2 (gfedcba[0], and_2_out, and_3_out, DCBA[1], DCBA[3]);
  or or_3 (gfedcba[1], and_4_out, and_5_out, not_3_out);
  and and_10 (and_10_out, and_3_out, not_2_out);
  or or_4 (gfedcba[4], and_2_out, and_6_out);
  or or_5 (gfedcba[5], DCBA[3], and_4_out, and_8_out, and_9_out);
  or or_6 (gfedcba[6], DCBA[3], and_8_out, and_6_out, and_1_out);
  or or_7 (gfedcba[3], and_6_out, and_1_out, and_2_out, and_7_out, and_10_out);
  _7_Segment_Display u_7_segment_display_1 (
    .g(gfedcba[6]), .f(gfedcba[5]), .a(gfedcba[0]), .b(gfedcba[1]), .e(gfedcba[4]), .d(gfedcba[3]),
    .c(gfedcba[2]));  // open: dp

  // Notes on the sheet:
  //   A
  //   B
  //   C
  //   D
  //   b
  //   a
  //   c
  //   d
  //   e
  //   f
  //   g
endmodule
