// Logisim project full-adder.circ as structural Verilog: 1 circuit, main circuit full-adder
module full_adder (
  input  Ai,
  input  Bi,
  input  Ci_1,
  output Si,
  output Ci
);

  wire and_1_out, and_2_out, xor_1_out;

  xor xor_1 (xor_1_out, Ai, Bi);
  and and_1 (and_1_out, xor_1_out, Ci_1);
  and and_2 (and_2_out, Bi, Ai);
  xor xor_2 (Si, xor_1_out, Ci_1);
  or or_1 (Ci, and_1_out, and_2_out);
endmodule
