// Logisim project half-adder.circ as structural Verilog: 1 circuit, main circuit half-adder
module half_adder (
  input  A,
  input  B,
  output S,
  output C
);

  xor xor_1 (S, A, B);
  and and_1 (C, B, A);
endmodule
