// Logisim project self-adder controller v1.0.circ as structural Verilog: 1 circuit, main circuit self-adder controller v1.0
module self_adder_controller_v1_0 (
  input  O7,
  input  O6,
  input  O5,
  input  O4,
  input  O3,
  input  O2,
  input  O1,
  input  O0,
  output CL,
  output CC,
  output DRW,
  output MS,
  output RE
);

  wire not_2_out;

  not not_1 (CC, O3);
  not not_2 (not_2_out, O3);
  and and_1 (DRW, not_2_out, O0);
  not not_3 (MS, O4);
  not not_4 (RE, O0);

  assign CL = 1'b1;
endmodule
