// Logisim project self-adder controller v1.1.circ as structural Verilog: 1 circuit, main circuit self-adder controller v1.1
module self_adder_controller_v1_1 (
  input  O7,
  input  O6,
  input  O5,
  input  O4,
  input  O3,
  input  O2,
  input  O1,
  input  O0,
  output CL,
  output CC,
  output DRW,
  output MS,
  output RE,
  output CI
);

  wire not_2_out, not_4_out, not_5_out;

  not not_1 (CC, O3);
  not not_2 (not_2_out, O5);
  and and_1 (DRW, not_2_out, O0);
  not not_3 (MS, O4);
  not not_4 (not_4_out, O4);
  or or_1 (RE, not_4_out, not_5_out);
  not not_5 (not_5_out, O0);

  assign CI = O0;
  assign CL = 1'b0;
endmodule
