// Logisim project self-adder controller v1.2.circ as structural Verilog: 1 circuit, main circuit self-adder controller v1.2
module self_adder_controller_v1_2 (
  input  O7,
  input  O6,
  input  O5,
  input  O4,
  input  O3,
  input  O2,
  input  O1,
  input  O0,
  output CL,
  output CC,
  output DRW,
  output MS,
  output RE,
  output SF,
  output CS1,
  output CS0
);

  wire not_2_out, not_4_out, not_5_out, not_6_out, not_7_out, not_8_out;

  not not_1 (CC, O3);
  not not_2 (not_2_out, O5);
  and and_1 (DRW, not_2_out, O0);
  not not_3 (MS, O4);
  not not_4 (not_4_out, O4);
  or or_1 (RE, not_4_out, not_5_out);
  not not_5 (not_5_out, O0);
  not not_6 (not_6_out, O1);
  and and_2 (CS1, not_6_out, O0);
  not not_7 (not_7_out, O1);
  and and_3 (CS0, not_7_out, not_8_out);
  not not_8 (not_8_out, O0);

  assign CL = 1'b0;
  assign SF = O0;
endmodule
