// Logisim project self-adder controller v2.1.circ as structural Verilog: 1 circuit, main circuit self-adder controller v2.1
module self_adder_controller_v2_1 (
  input  O7,
  input  O6,
  input  O5,
  input  O4,
  input  O3,
  input  O2,
  input  O1,
  input  O0,
  input  ENDT,
  output CL,
  output CC,
  output W,
  output ACS,
  output ACE,
  output SF,
  output CS1,
  output CS0,
  output CE,
  output ICE,
  output ADS
);

  wire and_4_out, and_5_out, not_1_out, not_2_out, not_3_out, not_4_out, not_6_out, not_7_out, not_8_out,
       not_9_out, not_10_out, not_11_out, not_12_out;

  not not_1 (not_1_out, O2);
  not not_2 (not_2_out, O2);
  not not_3 (not_3_out, ENDT);
  not not_4 (not_4_out, O5);
  not not_5 (ACS, O4);
  not not_6 (not_6_out, O5);
  not not_7 (not_7_out, O0);
  not not_8 (not_8_out, O4);
  not not_9 (not_9_out, O1);
  not not_10 (not_10_out, O1);
  not not_11 (not_11_out, O0);
  not not_12 (not_12_out, O4);
  not not_13 (ICE, O2);
  and and_1 (CL, O5, O4, not_1_out, ENDT);
  and and_2 (CC, not_2_out, not_3_out);
  and and_3 (W, not_4_out, O0, ENDT);
  and and_4 (and_4_out, not_6_out, not_7_out, ENDT);
  and and_5 (and_5_out, not_8_out, ENDT);
  and and_6 (CS1, not_9_out, O0);
  and and_7 (CS0, not_10_out, not_11_out);
  and and_8 (CE, not_12_out, ENDT);
  or or_1 (ACE, and_4_out, and_5_out);

  assign ADS = ENDT;
  assign SF = O0;
endmodule
