// Logisim project self-adder controller v2.2.circ as structural Verilog: 1 circuit, main circuit self-adder controller v2.2
module self_adder_controller_v2_2 (
  input  O7,
  input  O6,
  input  O5,
  input  O4,
  input  O3,
  input  O2,
  input  O1,
  input  O0,
  input  ENDT,
  input  ZF,
  input  CF,
  output CL,
  output CC,
  output W,
  output ACS,
  output ACE,
  output SF,
  output CS1,
  output CS0,
  output CE,
  output ICE,
  output ADS,
  output ZE
);

  wire and_3_out, and_4_out, and_9_out, and_10_out, and_11_out, and_12_out, and_13_out, not_1_out, not_2_out,
       not_3_out, not_4_out, not_5_out, not_6_out, not_7_out, not_8_out, not_9_out, not_10_out, not_11_out,
       not_12_out, not_13_out, not_14_out, not_15_out, not_16_out, not_17_out, not_18_out, not_19_out,
       not_20_out, not_22_out, not_23_out, not_24_out, not_25_out, not_26_out, not_27_out, not_28_out,
       not_30_out;

  not not_1 (not_1_out, O6);
  not not_2 (not_2_out, O2);
  not not_3 (not_3_out, O1);
  not not_4 (not_4_out, O0);
  not not_5 (not_5_out, O6);
  not not_6 (not_6_out, O2);
  not not_7 (not_7_out, O1);
  not not_8 (not_8_out, O6);
  not not_9 (not_9_out, O2);
  not not_10 (not_10_out, O0);
  not not_11 (not_11_out, O6);
  not not_12 (not_12_out, O2);
  not not_13 (not_13_out, ZF);
  not not_14 (not_14_out, O6);
  not not_15 (not_15_out, O1);
  not not_16 (not_16_out, O0);
  not not_17 (not_17_out, CF);
  not not_18 (not_18_out, O3);
  not not_19 (not_19_out, ENDT);
  not not_20 (not_20_out, O5);
  not not_21 (ACS, O4);
  not not_22 (not_22_out, O5);
  not not_23 (not_23_out, O0);
  not not_24 (not_24_out, O4);
  not not_25 (not_25_out, O1);
  not not_26 (not_26_out, O1);
  not not_27 (not_27_out, O0);
  not not_28 (not_28_out, O4);
  not not_29 (ICE, O3);
  not not_30 (not_30_out, O4);
  and and_1 (CC, not_18_out, not_19_out);
  and and_2 (W, not_20_out, O0, ENDT);
  and and_3 (and_3_out, not_22_out, not_23_out, ENDT);
  and and_4 (and_4_out, not_24_out, ENDT);
  and and_5 (CS1, not_25_out, O0);
  and and_6 (CS0, not_26_out, not_27_out);
  and and_7 (CE, not_28_out, ENDT);
  and and_8 (ZE, not_30_out, ENDT);
  and and_9 (and_9_out, not_1_out, O5, O4, not_2_out, not_3_out, not_4_out, ENDT);
  and and_10 (and_10_out, not_5_out, O5, O4, not_6_out, not_7_out, O0, ENDT, ZF);
  and and_11 (and_11_out, not_8_out, O5, O4, not_9_out, O1, not_10_out, ENDT, CF);
  and and_12 (and_12_out, not_11_out, O5, O4, not_12_out, O1, O0, ENDT, not_13_out);
  and and_13 (and_13_out, not_14_out, O5, O4, O2, not_15_out, not_16_out, ENDT, not_17_out);
  or or_1 (ACE, and_3_out, and_4_out);
  or or_2 (CL, and_9_out, and_10_out, and_11_out, and_12_out, and_13_out);

  assign ADS = ENDT;
  assign SF = O0;
endmodule
