// Logisim project 3bit_counter.circ as structural Verilog: 1 circuit, main circuit 3bit_counter
module _3bit_counter (
  input  in_1,
  output [2:0] out_2
);

  wire d_ff_1_qn, d_ff_2_qn;

  not not_1 (out_2[0], in_1);
  D_Flip_Flop d_ff_1 (.clk(in_1), .D(d_ff_1_qn), .Q(out_2[1]), .Qn(d_ff_1_qn));  // open: preset, en, reset
  D_Flip_Flop d_ff_2 (.clk(d_ff_1_qn), .D(d_ff_2_qn), .Q(out_2[2]), .Qn(d_ff_2_qn));  // open: preset, en, reset
endmodule
