// Logisim project 4-bit binary counter.circ as structural Verilog: 1 circuit, main circuit 4-bit binary counter
module _4_bit_binary_counter (
  input  Clk,
  output [3:0] Q0_3,
  output C
);

  wire and_1_out, and_2_out;

  and and_1 (and_1_out, Q0_3[1], Q0_3[0]);
  and and_2 (and_2_out, Q0_3[2], Q0_3[1], Q0_3[0]);
  and and_3 (C, Q0_3[3], Q0_3[2], Q0_3[1], Q0_3[0]);
  T_Flip_Flop FF0 (.clk(Clk), .T(1'b1), .Q(Q0_3[0]));  // open: Qn, preset, reset, en
  T_Flip_Flop FF1 (.clk(Clk), .T(Q0_3[0]), .Q(Q0_3[1]));  // open: Qn, preset, reset, en
  T_Flip_Flop FF2 (.clk(Clk), .T(and_1_out), .Q(Q0_3[2]));  // open: Qn, preset, reset, en
  T_Flip_Flop FF3 (.clk(Clk), .T(and_2_out), .Q(Q0_3[3]));  // open: Qn, preset, reset, en
endmodule
