// Logisim project 8x1 RAM.circ as structural Verilog: 1 circuit, main circuit 8x1 RAM
module _8x1_RAM (
  input  DI,
  input  [2:0] A2_0,
  input  W,
  output DO
);

  wire d_syn_1_q, d_syn_2_q, d_syn_3_q, d_syn_4_q, d_syn_5_q, d_syn_6_q, d_syn_7_q, d_syn_8_q, not_1_out;
  wire [7:0] n3_8_decoder_1_y_prime_7_0, not_2_out;

  not not_1 (not_1_out, W);
  _3_8_decoder u_3_8_decoder_1 (.I2_0(A2_0), .EN_prime(not_1_out), .Y_prime_7_0(n3_8_decoder_1_y_prime_7_0));
  assign not_2_out = ~n3_8_decoder_1_y_prime_7_0;  // NOT_Gate not_2, 8 bits wide
  D_syn d_syn_1 (.D(DI), .Q(d_syn_1_q), .Clk(not_2_out[0]));  // open: Q_prime
  D_syn d_syn_2 (.D(DI), .Q(d_syn_2_q), .Clk(not_2_out[1]));  // open: Q_prime
  D_syn d_syn_3 (.D(DI), .Q(d_syn_3_q), .Clk(not_2_out[2]));  // open: Q_prime
  D_syn d_syn_4 (.D(DI), .Q(d_syn_4_q), .Clk(not_2_out[3]));  // open: Q_prime
  D_syn d_syn_5 (.D(DI), .Q(d_syn_5_q), .Clk(not_2_out[4]));  // open: Q_prime
  D_syn d_syn_6 (.D(DI), .Q(d_syn_6_q), .Clk(not_2_out[5]));  // open: Q_prime
  D_syn d_syn_7 (.D(DI), .Q(d_syn_7_q), .Clk(not_2_out[6]));  // open: Q_prime
  D_syn d_syn_8 (.D(DI), .Q(d_syn_8_q), .Clk(not_2_out[7]));  // open: Q_prime
  _8_1_multiplexer u_8_1_multiplexer_1 (
    .D0(d_syn_1_q), .D1(d_syn_2_q), .D2(d_syn_3_q), .D3(d_syn_4_q), .D4(d_syn_5_q), .D5(d_syn_6_q),
    .D6(d_syn_7_q), .D7(d_syn_8_q), .A0(A2_0[0]), .A1(A2_0[1]), .A2(A2_0[2]), .EN_prime(1'b0), .Y(DO));

  // Notes on the sheet:
  //   8x1 RAM
  //   从上至下为第0位至第7位
endmodule
