// Logisim project 8x8 RAM.circ as structural Verilog: 1 circuit, main circuit 8x8 RAM
module _8x8_RAM (
  input  [2:0] A0_2,
  input  [7:0] DI0_7,
  input  W,
  output [7:0] DO0_7
);

  _8x1_RAM u_8x1_ram_1 (.DI(DI0_7[0]), .A2_0(A0_2), .W(W), .DO(DO0_7[0]));
  _8x1_RAM u_8x1_ram_2 (.DI(DI0_7[1]), .A2_0(A0_2), .W(W), .DO(DO0_7[1]));
  _8x1_RAM u_8x1_ram_3 (.DI(DI0_7[2]), .A2_0(A0_2), .W(W), .DO(DO0_7[2]));
  _8x1_RAM u_8x1_ram_4 (.DI(DI0_7[3]), .A2_0(A0_2), .W(W), .DO(DO0_7[3]));
  _8x1_RAM u_8x1_ram_5 (.DI(DI0_7[4]), .A2_0(A0_2), .W(W), .DO(DO0_7[4]));
  _8x1_RAM u_8x1_ram_6 (.DI(DI0_7[5]), .A2_0(A0_2), .W(W), .DO(DO0_7[5]));
  _8x1_RAM u_8x1_ram_7 (.DI(DI0_7[6]), .A2_0(A0_2), .W(W), .DO(DO0_7[6]));
  _8x1_RAM u_8x1_ram_8 (.DI(DI0_7[7]), .A2_0(A0_2), .W(W), .DO(DO0_7[7]));

  // Notes on the sheet:
  //   8x8 RAM
endmodule
