// Logisim project BCD counter.circ as structural Verilog: 1 circuit, main circuit BCD counter
module BCD_counter (
  input  Clk,
  output [3:0] Q0_3,
  output C
);

  wire and_1_out, and_2_out, and_3_out, and_4_out, or_1_out, t_ff_4_qn;

  and and_1 (and_1_out, Q0_3[0], t_ff_4_qn);
  and and_2 (and_2_out, Q0_3[1], Q0_3[0]);
  and and_3 (and_3_out, Q0_3[2], and_2_out);
  and and_4 (and_4_out, Q0_3[3], Q0_3[0]);
  or or_1 (or_1_out, and_3_out, and_4_out);
  T_Flip_Flop t_ff_1 (.clk(Clk), .T(1'b1), .Q(Q0_3[0]));  // open: Qn, preset, reset, en
  T_Flip_Flop t_ff_2 (.clk(Clk), .T(and_1_out), .Q(Q0_3[1]));  // open: Qn, preset, reset, en
  T_Flip_Flop t_ff_3 (.clk(Clk), .T(and_2_out), .Q(Q0_3[2]));  // open: Qn, preset, reset, en
  T_Flip_Flop t_ff_4 (.clk(Clk), .T(or_1_out), .Q(Q0_3[3]), .Qn(t_ff_4_qn));  // open: preset, reset, en
  and and_5 (C, Q0_3[0], Q0_3[3]);

  // Notes on the sheet:
  //   F0
  //   F1
  //   F2
  //   F3
endmodule
