// Logisim project D_base.circ as structural Verilog: 1 circuit, main circuit main
module main (
  input  in_1,
  output out_2,
  output out_3
);

  wire not_1_out;

  not not_1 (not_1_out, in_1);
  nor nor_1 (out_2, not_1_out, out_3);
  nor nor_2 (out_3, out_2, in_1);
endmodule
