// Logisim project D_edge.circ as structural Verilog: 1 circuit, main circuit D_edge
module D_edge (
  input  RD_prime,
  input  D,
  input  Clk,
  input  SD_prime,
  output Q_prime,
  output Q
);

  wire nand_1_out, nand_2_out, nand_3_out, nand_4_out;

  nand nand_1 (nand_1_out, RD_prime, D, nand_3_out);
  nand nand_2 (nand_2_out, nand_1_out, SD_prime, nand_4_out);
  nand nand_3 (nand_3_out, Clk, nand_1_out, nand_4_out);
  nand nand_4 (nand_4_out, RD_prime, nand_2_out, Clk);
  nand nand_5 (Q_prime, RD_prime, nand_3_out, Q);
  nand nand_6 (Q, Q_prime, nand_4_out, SD_prime);
endmodule
