// Logisim project D_syn.circ as structural Verilog: 1 circuit, main circuit D_syn
module D_syn (
  input  Clk,
  input  D,
  output Q_prime,
  output Q
);

  wire nand_1_out, nand_2_out, not_1_out;

  not not_1 (not_1_out, D);
  nand nand_1 (nand_1_out, not_1_out, Clk);
  nand nand_2 (nand_2_out, Clk, D);
  nand nand_3 (Q_prime, nand_1_out, Q);
  nand nand_4 (Q, Q_prime, nand_2_out);
endmodule
