// Logisim project JK_edge.circ as structural Verilog: 1 circuit, main circuit JK_edge
module JK_edge (
  input  J,
  input  Clk,
  input  K,
  input  in_4,
  input  in_5,
  output Q,
  output Q_2
);

  wire and_1_out, and_2_out, not_1_out, not_2_out, or_1_out;

  and and_1 (and_1_out, Q_2, J);
  not not_1 (not_1_out, Clk);
  not not_2 (not_2_out, K);
  and and_2 (and_2_out, not_2_out, Q);
  or or_1 (or_1_out, and_1_out, and_2_out);
  D_edge d_edge_1 (.RD_prime(in_4), .D(or_1_out), .SD_prime(in_5), .Q_prime(Q_2), .Q(Q), .Clk(not_1_out));
endmodule
