// Logisim project JK_lord.circ as structural Verilog: 1 circuit, main circuit main
module main (
  input  in_1,
  input  in_2,
  input  in_3,
  output out_4,
  output out_5
);

  wire and_1_out, and_2_out, and_3_out, and_4_out, clock_1_out, not_1_out, not_2_out, or_1_out, or_2_out,
       rs_syn_1_out_4, rs_syn_1_out_5;

  Clock clock_1 (.out(clock_1_out));
  not not_1 (not_1_out, in_3);
  and and_1 (and_1_out, in_3, and_2_out);
  and and_2 (and_2_out, in_1, out_5);
  and and_3 (and_3_out, out_4, in_2);
  RS_syn rs_syn_1 (
    .in_3(or_1_out), .out_4(rs_syn_1_out_4), .out_5(rs_syn_1_out_5), .in_1(and_1_out), .in_2(clock_1_out));
  or or_1 (or_1_out, and_3_out, not_1_out);
  not not_2 (not_2_out, clock_1_out);
  and and_4 (and_4_out, in_3, rs_syn_1_out_4);
  or or_2 (or_2_out, rs_syn_1_out_5, not_1_out);
  RS_syn rs_syn_2 (.in_3(or_2_out), .out_4(out_4), .out_5(out_5), .in_1(and_4_out), .in_2(not_2_out));
endmodule
