// Logisim project one digit loop.circ as structural Verilog: 1 circuit, main circuit one digit loop
module one_digit_loop (
  output [3:0] out_1
);

  wire clock_1_out;
  wire [6:0] bcd_7_seg_driver_decoder_1_gfedcba;

  Clock clock_1 (.out(clock_1_out));
  BCD_counter bcd_counter_1 (.Clk(clock_1_out), .Q0_3(out_1));  // open: C
  bcd_7_seg_driver_decoder bcd_7_seg_driver_decoder_1 (.DCBA(out_1), .gfedcba(bcd_7_seg_driver_decoder_1_gfedcba));
  _7_Segment_Display u_7_segment_display_1 (
    .g(bcd_7_seg_driver_decoder_1_gfedcba[6]), .f(bcd_7_seg_driver_decoder_1_gfedcba[5]),
    .a(bcd_7_seg_driver_decoder_1_gfedcba[0]), .b(bcd_7_seg_driver_decoder_1_gfedcba[1]),
    .e(bcd_7_seg_driver_decoder_1_gfedcba[4]), .d(bcd_7_seg_driver_decoder_1_gfedcba[3]),
    .c(bcd_7_seg_driver_decoder_1_gfedcba[2]));  // open: dp

  // Notes on the sheet:
  //   BCD counter
  //   7 seg driver
endmodule
