// Logisim project self-adder v2.0.circ as structural Verilog: 1 circuit, main circuit self-adder v2.0
module self_adder_v2_0 (
  input  O7,
  input  in_2,
  input  O6,
  input  O2,
  output [7:0] out_5,
  output [7:0] out_6,
  output [7:0] out_7
);

  wire ACE, ACS, adder_1_cout, ADS, CC, CE, Clk, CS0, CS1, decoder_1_out3, ENAD, ENOP, ICE,
       multiplexer_3_out, not_1_out, not_2_out, not_4_out, not_5_out, not_6_out, not_7_out, not_8_out,
       not_9_out, or_1_out, register_2_q, W;
  wire [1:0] counter_1_q;
  wire [7:0] adder_1_out, bit_extender_1_out, counter_2_q, DI, multiplexer_1_out, multiplexer_2_out,
       xor_1_out;

  Clock clock_1 (.out(Clk));
  Counter #(.width(2), .max('h2)) counter_1 (.Q(counter_1_q), .clk(Clk), .clr(in_2));  // open: load, D, count, carry
  Decoder #(.select(2), .disabled(0)) decoder_1 (
    .out0(ENOP), .out1(ENAD), .out2(ADS), .out3(decoder_1_out3), .sel(counter_1_q), .en(ICE));
  Counter counter_2 (.load(1'b0), .D(out_7), .count(CC), .Q(counter_2_q), .clk(Clk), .clr(in_2));  // open: carry
  Multiplexer #(.width(8)) multiplexer_1 (
    .in0(out_5), .in1(adder_1_out), .out(multiplexer_1_out), .sel(ACS));  // open: en
  Register register_1 (.D(multiplexer_1_out), .en(ACE), .Q(DI), .clk(Clk), .clr(in_2));
  Multiplexer #(.width(8)) multiplexer_2 (
    .in0(counter_2_q), .in1(out_7), .out(multiplexer_2_out), .sel(ADS));  // open: en
  assign bit_extender_1_out = {{7{out_6[0]}}, out_6[0]};  // Bit_Extender bit_extender_1
  assign out_5 = W ? DI : 8'bz;  // Controlled_Buffer controlled_buffer_1
  not not_1 (not_1_out, W);
  assign xor_1_out = bit_extender_1_out ^ out_5;  // XOR_Gate xor_1, 8 bits wide
  Adder adder_1 (.a(xor_1_out), .b(DI), .out(adder_1_out), .cin(multiplexer_3_out), .cout(adder_1_cout));
  Register #(.width(1)) register_2 (.D(adder_1_cout), .en(CE), .Q(register_2_q), .clk(Clk), .clr(in_2));
  RAM ram_1 (.addr(multiplexer_2_out), .data(out_5), .clk(Clk), .ld(not_1_out));  // open: sel, clr
  Multiplexer #(.select(2)) multiplexer_3 (
    .in0(register_2_q), .in1(1'b0), .in2(1'b1), .out(multiplexer_3_out), .sel({CS1, CS0}));  // open: in3, en
  Register register_3 (.D(out_5), .en(ENOP), .Q(out_6), .clk(Clk), .clr(in_2));
  Register register_4 (.D(out_5), .en(ENAD), .Q(out_7), .clk(Clk), .clr(in_2));
  nor nor_1 (CC, ADS, out_6[3]);
  not not_2 (not_2_out, out_6[5]);
  and and_1 (W, not_2_out, ADS, out_6[0]);
  not not_3 (ACS, out_6[4]);
  not not_4 (not_4_out, out_6[4]);
  or or_1 (or_1_out, not_4_out, not_5_out);
  not not_5 (not_5_out, out_6[0]);
  not not_6 (not_6_out, out_6[1]);
  and and_2 (CS1, not_6_out, out_6[0]);
  not not_7 (not_7_out, out_6[1]);
  and and_3 (CS0, not_7_out, not_8_out);
  not not_8 (not_8_out, out_6[0]);
  not not_9 (not_9_out, out_6[4]);
  and and_4 (CE, not_9_out, ADS);
  not not_10 (ICE, out_6[3]);
  and and_5 (ACE, or_1_out, ADS);

  // Other names for the same wires on the sheet: ADcode[7:0] = out_7; Clr = in_2; DO[7:0] = out_5; ENDT = ADS;
  //   OPcode[7:0] = out_6; SF = out_6[0]

  // Notes on the sheet:
  //   Program Counter
  //   Accumulator
  //   Instruction cycle decoder
  //   (Arithmetic Unit)
  //   Carry Register
  //   Data/Progame RAM
  //   (Memory)
  //   Operation Code Register
  //   Address Code Register
  //   O5
  //   O4
  //   O3
  //   O1
  //   O0
  //   (Controller)
endmodule
