// Logisim project self-adder v2.1.circ as structural Verilog: 1 circuit, main circuit self-adder v2.1
module self_adder_v2_1 (
  input  in_1,
  output [7:0] out_2,
  output [7:0] out_3,
  output [7:0] out_4
);

  wire ACE, ACS, adder_1_cout, ADS, and_4_out, and_5_out, CC, CE, CL, Clk, CS0, CS1, decoder_1_out3, ENAD,
       ENOP, ICE, multiplexer_3_out, not_1_out, not_2_out, not_3_out, not_4_out, not_5_out, not_7_out,
       not_8_out, not_9_out, not_10_out, not_11_out, not_12_out, not_13_out, register_2_q, W;
  wire [1:0] counter_1_q;
  wire [7:0] adder_1_out, bit_extender_1_out, counter_2_q, DI, multiplexer_1_out, multiplexer_2_out,
       xor_1_out;

  Clock clock_1 (.out(Clk));
  Counter #(.width(2), .max('h2)) counter_1 (.Q(counter_1_q), .clk(Clk), .clr(in_1));  // open: load, D, count, carry
  Decoder #(.select(2), .disabled(0)) decoder_1 (
    .out0(ENOP), .out1(ENAD), .out2(ADS), .out3(decoder_1_out3), .sel(counter_1_q), .en(ICE));
  Counter counter_2 (.load(CL), .D(out_4), .count(CC), .Q(counter_2_q), .clk(Clk), .clr(in_1));  // open: carry
  Register register_1 (.D(multiplexer_1_out), .en(ACE), .Q(DI), .clk(Clk), .clr(in_1));
  Multiplexer #(.width(8)) multiplexer_1 (
    .in0(out_2), .in1(adder_1_out), .out(multiplexer_1_out), .sel(ACS));  // open: en
  Multiplexer #(.width(8)) multiplexer_2 (
    .in0(counter_2_q), .in1(out_4), .out(multiplexer_2_out), .sel(ADS));  // open: en
  assign bit_extender_1_out = {{7{out_3[0]}}, out_3[0]};  // Bit_Extender bit_extender_1
  assign out_2 = W ? DI : 8'bz;  // Controlled_Buffer controlled_buffer_1
  not not_1 (not_1_out, W);
  assign xor_1_out = bit_extender_1_out ^ out_2;  // XOR_Gate xor_1, 8 bits wide
  Adder adder_1 (.a(xor_1_out), .b(DI), .out(adder_1_out), .cin(multiplexer_3_out), .cout(adder_1_cout));
  Register #(.width(1)) register_2 (.D(adder_1_cout), .en(CE), .Q(register_2_q), .clk(Clk), .clr(in_1));
  RAM ram_1 (.addr(multiplexer_2_out), .data(out_2), .clk(Clk), .ld(not_1_out));  // open: sel, clr
  Multiplexer #(.select(2)) multiplexer_3 (
    .in0(register_2_q), .in1(1'b0), .in2(1'b1), .out(multiplexer_3_out), .sel({CS1, CS0}));  // open: in3, en
  Register register_3 (.D(out_2), .en(ENOP), .Q(out_3), .clk(Clk), .clr(in_1));
  Register register_4 (.D(out_2), .en(ENAD), .Q(out_4), .clk(Clk), .clr(in_1));
  not not_2 (not_2_out, out_3[2]);
  not not_3 (not_3_out, out_3[2]);
  not not_4 (not_4_out, ADS);
  not not_5 (not_5_out, out_3[5]);
  not not_6 (ACS, out_3[4]);
  not not_7 (not_7_out, out_3[5]);
  not not_8 (not_8_out, out_3[0]);
  not not_9 (not_9_out, out_3[4]);
  not not_10 (not_10_out, out_3[1]);
  not not_11 (not_11_out, out_3[1]);
  not not_12 (not_12_out, out_3[0]);
  not not_13 (not_13_out, out_3[4]);
  not not_14 (ICE, out_3[2]);
  and and_1 (CL, out_3[5], out_3[4], not_2_out, ADS);
  and and_2 (CC, not_3_out, not_4_out);
  and and_3 (W, not_5_out, out_3[0], ADS);
  and and_4 (and_4_out, not_7_out, not_8_out, ADS);
  and and_5 (and_5_out, not_9_out, ADS);
  and and_6 (CS1, not_10_out, out_3[0]);
  and and_7 (CS0, not_11_out, not_12_out);
  and and_8 (CE, not_13_out, ADS);
  or or_1 (ACE, and_4_out, and_5_out);

  // Other names for the same wires on the sheet: ADcode[7:0] = out_4; Clr = in_1; DO[7:0] = out_2; ENDT = ADS;
  //   OPcode[7:0] = out_3; SF = out_3[0]

  // Notes on the sheet:
  //   Program Counter
  //   Accumulator
  //   Instruction cycle decoder
  //   (Arithmetic Unit)
  //   Carry Register
  //   Data/Progame RAM
  //   (Memory)
  //   Operation Code Register
  //   Address Code Register
  //   (Controller)
endmodule
