// Logisim project self-adder v2.2.circ as structural Verilog: 1 circuit, main circuit self-adder v2.2
module self_adder_v2_2 (
  input  in_1,
  output [7:0] out_2,
  output [7:0] out_3,
  output [7:0] out_4
);

  wire ACE, ACS, adder_1_cout, ADS, and_1_out, and_2_out, and_3_out, and_4_out, and_5_out, and_8_out,
       and_9_out, CC, CE, CF, CL, Clk, CS0, CS1, decoder_1_out3, ENAD, ENOP, ICE, multiplexer_3_out,
       nor_1_out, not_1_out, not_2_out, not_3_out, not_4_out, not_5_out, not_6_out, not_7_out, not_8_out,
       not_9_out, not_10_out, not_11_out, not_12_out, not_13_out, not_14_out, not_15_out, not_16_out,
       not_17_out, not_18_out, not_19_out, not_20_out, not_21_out, not_23_out, not_24_out, not_25_out,
       not_26_out, not_27_out, not_28_out, not_29_out, not_31_out, W, ZE, ZF;
  wire [1:0] counter_1_q;
  wire [7:0] adder_1_out, bit_extender_1_out, counter_2_q, DI, multiplexer_1_out, multiplexer_2_out,
       xor_1_out;

  Clock clock_1 (.out(Clk));
  Counter #(.width(2), .max('h2)) counter_1 (.Q(counter_1_q), .clk(Clk), .clr(in_1));  // open: load, D, count, carry
  Decoder #(.select(2), .disabled(0)) decoder_1 (
    .out0(ENOP), .out1(ENAD), .out2(ADS), .out3(decoder_1_out3), .sel(counter_1_q), .en(ICE));
  Counter counter_2 (.load(CL), .D(out_4), .count(CC), .Q(counter_2_q), .clk(Clk), .clr(in_1));  // open: carry
  Multiplexer #(.width(8)) multiplexer_1 (
    .in0(out_2), .in1(adder_1_out), .out(multiplexer_1_out), .sel(ACS));  // open: en
  Register register_1 (.D(multiplexer_1_out), .en(ACE), .Q(DI), .clk(Clk), .clr(in_1));
  Multiplexer #(.width(8)) multiplexer_2 (
    .in0(counter_2_q), .in1(out_4), .out(multiplexer_2_out), .sel(ADS));  // open: en
  assign bit_extender_1_out = {{7{out_3[0]}}, out_3[0]};  // Bit_Extender bit_extender_1
  assign out_2 = W ? DI : 8'bz;  // Controlled_Buffer controlled_buffer_1
  not not_1 (not_1_out, W);
  assign xor_1_out = bit_extender_1_out ^ out_2;  // XOR_Gate xor_1, 8 bits wide
  Adder adder_1 (.a(xor_1_out), .b(DI), .out(adder_1_out), .cin(multiplexer_3_out), .cout(adder_1_cout));
  Register #(.width(1)) register_2 (.D(adder_1_cout), .en(CE), .Q(CF), .clk(Clk), .clr(in_1));
  RAM ram_1 (.addr(multiplexer_2_out), .data(out_2), .clk(Clk), .ld(not_1_out));  // open: sel, clr
  Multiplexer #(.select(2)) multiplexer_3 (
    .in0(CF), .in1(1'b0), .in2(1'b1), .out(multiplexer_3_out), .sel({CS1, CS0}));  // open: in3, en
  Register register_3 (.D(out_2), .en(ENOP), .Q(out_3), .clk(Clk), .clr(in_1));
  Register register_4 (.D(out_2), .en(ENAD), .Q(out_4), .clk(Clk), .clr(in_1));
  nor nor_1 (nor_1_out, adder_1_out[0], adder_1_out[1], adder_1_out[2], adder_1_out[3], adder_1_out[4], adder_1_out[5], adder_1_out[6], adder_1_out[7]);
  Register #(.width(1)) register_5 (.D(nor_1_out), .en(ZE), .Q(ZF), .clk(Clk), .clr(in_1));
  not not_2 (not_2_out, out_3[6]);
  not not_3 (not_3_out, out_3[2]);
  not not_4 (not_4_out, out_3[1]);
  not not_5 (not_5_out, out_3[0]);
  not not_6 (not_6_out, out_3[6]);
  not not_7 (not_7_out, out_3[2]);
  not not_8 (not_8_out, out_3[1]);
  not not_9 (not_9_out, out_3[6]);
  not not_10 (not_10_out, out_3[2]);
  not not_11 (not_11_out, out_3[0]);
  not not_12 (not_12_out, out_3[6]);
  not not_13 (not_13_out, out_3[2]);
  not not_14 (not_14_out, ZF);
  not not_15 (not_15_out, out_3[6]);
  not not_16 (not_16_out, out_3[1]);
  not not_17 (not_17_out, out_3[0]);
  not not_18 (not_18_out, CF);
  not not_19 (not_19_out, out_3[3]);
  not not_20 (not_20_out, ADS);
  not not_21 (not_21_out, out_3[5]);
  not not_22 (ACS, out_3[4]);
  not not_23 (not_23_out, out_3[5]);
  not not_24 (not_24_out, out_3[0]);
  not not_25 (not_25_out, out_3[4]);
  not not_26 (not_26_out, out_3[1]);
  not not_27 (not_27_out, out_3[1]);
  not not_28 (not_28_out, out_3[0]);
  not not_29 (not_29_out, out_3[4]);
  not not_30 (ICE, out_3[3]);
  not not_31 (not_31_out, out_3[4]);
  and and_1 (and_1_out, not_2_out, out_3[5], out_3[4], not_3_out, not_4_out, not_5_out, ADS);
  and and_2 (and_2_out, not_6_out, out_3[5], out_3[4], not_7_out, not_8_out, out_3[0], ADS, ZF);
  and and_3 (and_3_out, not_9_out, out_3[5], out_3[4], not_10_out, out_3[1], not_11_out, ADS, CF);
  and and_4 (and_4_out, not_12_out, out_3[5], out_3[4], not_13_out, out_3[1], out_3[0], ADS, not_14_out);
  and and_5 (and_5_out, not_15_out, out_3[5], out_3[4], out_3[2], not_16_out, not_17_out, ADS, not_18_out);
  and and_6 (CC, not_19_out, not_20_out);
  and and_7 (W, not_21_out, out_3[0], ADS);
  and and_8 (and_8_out, not_23_out, not_24_out, ADS);
  and and_9 (and_9_out, not_25_out, ADS);
  and and_10 (CS1, not_26_out, out_3[0]);
  and and_11 (CS0, not_27_out, not_28_out);
  and and_12 (CE, not_29_out, ADS);
  and and_13 (ZE, not_31_out, ADS);
  or or_1 (CL, and_1_out, and_2_out, and_3_out, and_4_out, and_5_out);
  or or_2 (ACE, and_8_out, and_9_out);

  // Other names for the same wires on the sheet: ADcode[7:0] = out_4; Clr = in_1; DO[7:0] = out_2; ENDT = ADS;
  //   OPcode[7:0] = out_3; SF = out_3[0]

  // Notes on the sheet:
  //   Program Counter
  //   Accumulator
  //   Instruction cycle decoder
  //   (Arithmetic Unit)
  //   Carry Register
  //   Data/Progame RAM
  //   (Memory)
  //   Operation Code Register
  //   Address Code Register
  //   Zero Register
  //   (Controller)
endmodule
