// Logisim project self_adder v1.0.circ as structural Verilog: 1 circuit, main circuit self_adder v1.0
module self_adder_v1_0 (
  input  CLR,
  output [7:0] out_2,
  output [7:0] out_3
);

  wire CC, clock_1_out, DRW, MS, not_1_out, not_2_out, not_3_out, RE;
  wire [7:0] adder_1_out, counter_1_q, multiplexer_1_out, register_1_q;

  Clock clock_1 (.out(clock_1_out));
  Counter counter_1 (.load(1'b0), .count(CC), .Q(counter_1_q), .clk(clock_1_out), .clr(CLR));  // open: D, carry
  assign out_3 = DRW ? register_1_q : 8'bz;  // Controlled_Buffer controlled_buffer_1
  not not_1 (not_1_out, DRW);
  RAM ram_1 (.addr(counter_1_q), .data(out_2));  // open: sel, clk, ld, clr
  RAM ram_2 (.addr(counter_1_q), .data(out_3), .clk(clock_1_out), .ld(not_1_out));  // open: sel, clr
  Multiplexer #(.width(8)) multiplexer_1 (
    .in0(out_3), .in1(adder_1_out), .out(multiplexer_1_out), .sel(MS));  // open: en
  not not_2 (not_2_out, out_2[4]);
  not not_3 (not_3_out, out_2[5]);
  Register register_1 (.D(multiplexer_1_out), .en(RE), .Q(register_1_q), .clk(clock_1_out), .clr(CLR));
  not not_4 (CC, out_2[7]);
  Adder adder_1 (.a(out_3), .b(register_1_q), .out(adder_1_out));  // open: cin, cout
  and and_1 (DRW, out_2[0], out_2[4], not_3_out);
  and and_2 (MS, out_2[5], not_2_out);
  nor nor_1 (RE, out_2[0], out_2[6], out_2[7]);

  // Other names for the same wires on the sheet: OPcode[7:0] = out_2

  // Notes on the sheet:
  //   Prog RAM
  //   Data RAM
endmodule
