// Logisim project self_adder v1.1.circ as structural Verilog: 1 circuit, main circuit self_adder v1.1
module self_adder_v1_1 (
  input  CLR,
  output [7:0] out_2,
  output [7:0] out_3
);

  wire CC, clock_1_out, DRW, MS, not_1_out, not_3_out, not_5_out, not_6_out, RE;
  wire [7:0] adder_1_out, bit_extender_1_out, counter_1_q, multiplexer_1_out, register_1_q, xor_1_out;

  Clock clock_1 (.out(clock_1_out));
  Counter counter_1 (.load(1'b0), .count(CC), .Q(counter_1_q), .clk(clock_1_out), .clr(CLR));  // open: D, carry
  assign out_3 = DRW ? register_1_q : 8'bz;  // Controlled_Buffer controlled_buffer_1
  not not_1 (not_1_out, DRW);
  RAM ram_1 (.addr(counter_1_q), .data(out_2));  // open: sel, clk, ld, clr
  RAM ram_2 (.addr(counter_1_q), .data(out_3), .clk(clock_1_out), .ld(not_1_out));  // open: sel, clr
  Multiplexer #(.width(8)) multiplexer_1 (
    .in0(out_3), .in1(adder_1_out), .out(multiplexer_1_out), .sel(MS));  // open: en
  assign bit_extender_1_out = {{7{out_2[0]}}, out_2[0]};  // Bit_Extender bit_extender_1
  assign xor_1_out = bit_extender_1_out ^ out_3;  // XOR_Gate xor_1, 8 bits wide
  Register register_1 (.D(multiplexer_1_out), .en(RE), .Q(register_1_q), .clk(clock_1_out), .clr(CLR));
  Adder adder_1 (.a(xor_1_out), .b(register_1_q), .out(adder_1_out), .cin(out_2[0]));  // open: cout
  not not_2 (CC, out_2[3]);
  not not_3 (not_3_out, out_2[5]);
  not not_4 (MS, out_2[4]);
  not not_5 (not_5_out, out_2[4]);
  not not_6 (not_6_out, out_2[0]);
  and and_1 (DRW, out_2[0], not_3_out);
  or or_1 (RE, not_5_out, not_6_out);

  // Other names for the same wires on the sheet: CI = out_2[0]; OPcode[7:0] = out_2

  // Notes on the sheet:
  //   Prog RAM
  //   Data RAM
endmodule
