// Logisim project self_adder v1.2.circ as structural Verilog: 1 circuit, main circuit self-adder v1.2
module self_adder_v1_2 (
  input  O7,
  input  O6,
  input  CLR,
  input  O2,
  output [7:0] out_5,
  output [7:0] out_6
);

  wire adder_1_cout, CC, CE, clock_1_out, CS0, CS1, DRW, MS, multiplexer_2_out, not_1_out, not_3_out,
       not_5_out, not_6_out, not_7_out, not_8_out, not_9_out, RE, register_2_q;
  wire [7:0] adder_1_out, bit_extender_1_out, counter_1_q, multiplexer_1_out, register_1_q, xor_1_out;

  Clock clock_1 (.out(clock_1_out));
  Counter counter_1 (.load(1'b0), .count(CC), .Q(counter_1_q), .clk(clock_1_out), .clr(CLR));  // open: D, carry
  assign out_6 = DRW ? register_1_q : 8'bz;  // Controlled_Buffer controlled_buffer_1
  not not_1 (not_1_out, DRW);
  RAM ram_1 (.addr(counter_1_q), .data(out_5));  // open: sel, clk, ld, clr
  RAM ram_2 (.addr(counter_1_q), .data(out_6), .clk(clock_1_out), .ld(not_1_out));  // open: sel, clr
  Multiplexer #(.width(8)) multiplexer_1 (
    .in0(out_6), .in1(adder_1_out), .out(multiplexer_1_out), .sel(MS));  // open: en
  assign bit_extender_1_out = {{7{out_5[0]}}, out_5[0]};  // Bit_Extender bit_extender_1
  assign xor_1_out = bit_extender_1_out ^ out_6;  // XOR_Gate xor_1, 8 bits wide
  Register register_1 (.D(multiplexer_1_out), .en(RE), .Q(register_1_q), .clk(clock_1_out), .clr(CLR));
  Adder adder_1 (.a(xor_1_out), .b(register_1_q), .out(adder_1_out), .cin(multiplexer_2_out), .cout(adder_1_cout));
  Register #(.width(1)) register_2 (.D(adder_1_cout), .en(CE), .Q(register_2_q), .clk(clock_1_out), .clr(CLR));
  Multiplexer #(.select(2)) multiplexer_2 (
    .in0(register_2_q), .in1(1'b0), .in2(1'b1), .out(multiplexer_2_out), .sel({CS1, CS0}));  // open: in3, en
  not not_2 (CC, out_5[3]);
  not not_3 (not_3_out, out_5[5]);
  not not_4 (MS, out_5[4]);
  not not_5 (not_5_out, out_5[4]);
  not not_6 (not_6_out, out_5[0]);
  not not_7 (not_7_out, out_5[1]);
  not not_8 (not_8_out, out_5[1]);
  not not_9 (not_9_out, out_5[0]);
  not not_10 (CE, out_5[4]);
  and and_1 (DRW, not_3_out, out_5[0]);
  or or_1 (RE, not_5_out, not_6_out);
  and and_2 (CS1, not_7_out, out_5[0]);
  and and_3 (CS0, not_8_out, not_9_out);

  // Other names for the same wires on the sheet: OPcode[7:0] = out_5; SF = out_5[0]

  // Notes on the sheet:
  //   Prog RAM
  //   Data RAM
  //   Acc
  //   CF
  //   O5
  //   O4
  //   O3
  //   O1
  //   O0
endmodule
